# Fritzing sketch ground_station (saved by Fritzing 1.0.1rc)

parts:
  Raspberry_PI_4_Model_B = Raspberry Pi 4B
  ANT1 = Antenna
  LoRa_Module1 = Ra-01 - LoRa Module SX1278 [part_number=SX1278]

nets:
  3V3: Raspberry_PI_4_Model_B.3V3, LoRa_Module1.3.3V
  N1: Raspberry_PI_4_Model_B.GND, LoRa_Module1.GND#10
  N2: Raspberry_PI_4_Model_B.GPIO24, LoRa_Module1.DIO0
  N3: Raspberry_PI_4_Model_B.GPIO10, LoRa_Module1.MOSI
  N4: Raspberry_PI_4_Model_B.GPIO9, LoRa_Module1.MISO
  N5: Raspberry_PI_4_Model_B.GPIO25, LoRa_Module1.RESET
  N6: Raspberry_PI_4_Model_B.GPIO11, LoRa_Module1.SCK
  N7: Raspberry_PI_4_Model_B.GPIO8, LoRa_Module1.NSS
  N8: ANT1.antenna_lead, LoRa_Module1.ANT

custom parts:
  Ra-01 - LoRa Module SX1278: The Ra-01 LoRa Module featuring the SX1278 engine by Semtech. Module by AI-Thinker. Module (Ra-01) specifications from: https://www.banggood.com/Ra-01-Smart-Electronics-SX1278-LoRa-Spread-Spectrum-Wireless-Module-Ultra-Far-10KM-433M-p-1130769.html Description: Power supply: DC1.8-3.7V(3.3V) Chip: SX1278 Frequency: 433Mhz Operating temperature: -40~+85°C On Sheild Description (may vary by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
