# Fritzing sketch honeypot_node (saved by Fritzing 1.0.1rc)

parts:
  U1 = ESP32-38PinWide [part_number=ESP32-38PinWide]
  LoRa_Module1 = Ra-01 - LoRa Module SX1278 [part_number=SX1278]
  ANT1 = Antenna
  INA219 = Adafruit INA219 [part_number="Adafruit #904"]
  C1 = Ceramic Capacitor [capacitance="100 nF" voltage=35V package="0805 [SMD, multilayer]"]
  C2 = Electrolytic Capacitor [capacitance=47µF voltage=16V package="100 mil [THT, electrolytic]"]
  LED3 = LED - 3mm [color="Green (555nm)" current=0.030 package="3 mm [THT]"]
  LED2 = LED - 3mm [color="Yellow (574nm)" current=0.030 package="3 mm [THT]"]
  LED4 = LED - 3mm [color="Blue (430nm)" current=0.030 package="3 mm [THT]"]
  LED1 = LED - 3mm [color="Red (633nm)" current=0.030 package="3 mm [THT]"]
  R1 = Resistor [tolerance=±5% power=0.25 resistance=220 package=THT]
  R2 = Resistor [tolerance=±5% power=0.25 resistance=100 package=THT]
  R3 = Resistor [tolerance=±5% power=0.25 resistance=220 package=THT]
  R4 = Resistor [tolerance=±5% power=0.25 resistance=220 package=THT]

nets:
  N1: U1.3.3, INA219.VCC, INA219.VIN+
  N2: U1.GPIO32, R1.Pin_0
  N3: U1.GPIO26, LoRa_Module1.DIO0
  N4: U1.GPIO14, LoRa_Module1.RESET
  GND: U1.GND, LoRa_Module1.GND, INA219.GND, LED3.cathode, LED2.cathode, LED4.cathode, LED1.cathode
  N5: U1.GPIO4, R4.Pin_0
  N6: U1.GPIO16, R3.Pin_0
  N7: U1.GPIO17, R2.Pin_0
  N8: U1.GPIO5, LoRa_Module1.NSS
  N9: U1.GPIO18, LoRa_Module1.SCK
  N10: U1.GPIO19, LoRa_Module1.MISO
  N11: U1.GPIO21, INA219.SDA
  N12: U1.GPIO22, INA219.SCL
  N13: U1.GPIO23, LoRa_Module1.MOSI
  N14: LoRa_Module1.ANT, ANT1.antenna_lead
  N15: LoRa_Module1.3.3V, INA219.VIN-
  N16: C1.0, C2.-
  N17: C1.1, C2.+
  N18: LED3.anode, R3.Pin_1
  N19: LED2.anode, R2.Pin_1
  N20: LED4.anode, R4.Pin_1
  N21: LED1.anode, R1.Pin_1

custom parts:
  ESP32-38PinWide: Generic 38-Pin ESP32 with wide format (only access to one side of pins on a breadboard) based on Stephen Lilley's HiLetgo ESP-WROOM-32 ESP32 ESP-32S Development Board.
  Ra-01 - LoRa Module SX1278: The Ra-01 LoRa Module featuring the SX1278 engine by Semtech. Module by AI-Thinker. Module (Ra-01) specifications from: https://www.banggood.com/Ra-01-Smart-Electronics-SX1278-LoRa-Spread-Spectrum-Wireless-Module-Ultra-Far-10KM-433M-p-1130769.html Description: Power supply: DC1.8-3.7V(3.3V) Chip: SX1278 Frequency: 433Mhz Operating temperature: -40~+85°C On Sheild Description (may vary by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
  Adafruit INA219: This breakout board will solve all your power-monitoring problems. Instead of struggling with two multimeters, you can just use the handy INA219B chip on this breakout to both measure both the high side voltage and DC current draw over I2C with 1% precision. Most current-measuring devices such as our current panel meter are only good for low side measuring. That means that unless you want to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
