# Fritzing sketch uplink_transmitter (saved by Fritzing 1.0.1rc)

parts:
  U1 = DRF1278F LoRa/FSK Module (SX1278, 433 MHz) [part_number=DRF1278F]
  Raspberry_PI_Pico = Raspberry Pi Pico
  C1 = Ceramic Capacitor [capacitance="100 nF" voltage=35V package="0805 [SMD, multilayer]"]
  C2 = Electrolytic Capacitor [capacitance=47µF voltage=16V package="100 mil [THT, electrolytic]"]

nets:
  N1: U1.RESET, Raspberry_PI_Pico.pin_29
  N2: U1.DIO0, Raspberry_PI_Pico.pin_27
  N3: U1.VCC, Raspberry_PI_Pico.pin_36, C1.1, C2.+
  N4: U1.GND, Raspberry_PI_Pico.pin_3, Raspberry_PI_Pico.pin_33, C1.0, C2.-
  N5: U1.SCK, Raspberry_PI_Pico.pin_24
  N6: U1.MISO, Raspberry_PI_Pico.pin_26
  N7: U1.MOSI, Raspberry_PI_Pico.pin_25
  N8: U1.NSS, Raspberry_PI_Pico.pin_22

custom parts:
  DRF1278F LoRa/FSK Module (SX1278, 433 MHz): Dorji DRF1278F RF front-end module (Semtech SX1278), 17 x 17 mm, 15 castellated pads at 1.27 mm pitch, 1.8-3.6 V. Pin order from the DRF1278F datasheet Rev 1.1.
  Raspberry Pi Pico: Raspberry Pi Pico. Based around the RP2040 microcontroller the Pico is a low cost microcontroller device bringing Raspberry Pi quality, cost, and easy of use to the microcontroller space. Jan 2021, Split part in to two versions: tht (this one) and SMD. This one will drill holes for a .1 in header in pcb to allow plugging in the module as well as providing pads to solder the module to the top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
